# Fritzing sketch MorseCode (saved by Fritzing 0.9.3b)
breadboards: 1

parts:
  Part1 = Arduino Uno (Rev3)
  LCD1 = LCD screen
  R1 = Resistor [tolerance=±5% resistance=220 package=THT]
  S1 = Pushbutton [package="[THT]"]
  R2 = Trimmer Potentiometer [maximum_resistance=10kΩ package=THT]

nets:
  N1: Part1.D11_PWM/MOSI, LCD1.E
  N2: Part1.D12/MISO, LCD1.RS
  N3: Part1.GND, LCD1.R/W, LCD1.LED-, S1.Pin_1, S1.Pin_2, R2.leg2
  N4: Part1.D2, LCD1.DB7
  N5: Part1.D3_PWM, LCD1.DB6
  N6: Part1.D4, LCD1.DB5
  N7: Part1.D5_PWM, LCD1.DB4
  N8: Part1.D7, S1.Pin_3, S1.Pin_4
  N9: Part1.5V, R1.Pin_0, R2.leg1
  N10: LCD1.V0, R2.wiper
  N11: LCD1.LED+, R1.Pin_1
